// Logisim project control-logic.circ as structural Verilog: 1 circuit, main circuit control_logic
module control_logic (
  input  [31:0] Instruction,
  input  BrEq,
  input  BrLt,
  output PCSel,
  output RegWEn,
  output [2:0] ImmSel,
  output BrUn,
  output ASel,
  output BSel,
  output [3:0] ALUSel,
  output MemWEn,
  output [1:0] WBSel
);

  wire and_8_out, and_9_out, and_10_out, and_14_out, and_15_out, and_16_out, and_19_out, and_20_out,
       and_21_out, and_22_out, and_25_out, is_addi, is_andi, is_auipc, is_B_type, is_I_type, is_J_type,
       is_lui, is_ori, is_S_type, is_slli, is_slti, is_srai, is_srli, is_U_type, is_xori;
  wire [2:0] multiplexer_1_out, multiplexer_2_out, multiplexer_3_out, multiplexer_4_out, undriven;
  wire [3:0] bit_extender_1_out, ItypeSel;

  or or_1 (PCSel, BrEq, BrLt);
  and and_1 (is_I_type, Instruction[0], Instruction[1], ~Instruction[2], ~Instruction[3], Instruction[4], ~Instruction[5], ~Instruction[6]);  // AND_Gate
  and and_2 (is_S_type, Instruction[0], ~Instruction[1], ~Instruction[2], ~Instruction[3], ~Instruction[4], Instruction[5], ~Instruction[6]);  // AND_Gate
  and and_3 (is_B_type, Instruction[0], ~Instruction[1], ~Instruction[2], ~Instruction[3], ~Instruction[4], ~Instruction[5], Instruction[6]);  // AND_Gate
  and and_4 (is_auipc, Instruction[0], ~Instruction[1], ~Instruction[2], ~Instruction[3], Instruction[4], ~Instruction[5], ~Instruction[6]);  // AND_Gate
  and and_5 (is_lui, Instruction[0], Instruction[1], Instruction[2], ~Instruction[3], ~Instruction[4], Instruction[5], ~Instruction[6]);  // AND_Gate
  and and_6 (is_J_type, Instruction[0], Instruction[1], Instruction[2], Instruction[3], ~Instruction[4], Instruction[5], Instruction[6]);  // AND_Gate
  and and_7 (is_U_type, is_auipc, is_lui);
  and and_8 (and_8_out, ~Instruction[12], ~Instruction[13], ~Instruction[14]);  // AND_Gate
  and and_9 (and_9_out, Instruction[12], Instruction[13], Instruction[14]);
  and and_10 (and_10_out, ~Instruction[12], Instruction[13], Instruction[14]);  // AND_Gate
  and and_11 (is_addi, is_I_type, and_8_out);
  and and_12 (is_andi, is_I_type, and_9_out);
  and and_13 (is_ori, is_I_type, and_10_out);
  Multiplexer #(.width(3)) multiplexer_1 (.in0(undriven), .in1(3'b100), .out(multiplexer_1_out), .sel(is_J_type));
  buf or_2 (RegWEn, is_I_type);  // OR_Gate
  Multiplexer #(.width(3)) multiplexer_2 (
    .in0(multiplexer_1_out), .in1(3'b011), .out(multiplexer_2_out), .sel(is_U_type));
  Multiplexer #(.width(3)) multiplexer_3 (
    .in0(multiplexer_2_out), .in1(3'b010), .out(multiplexer_3_out), .sel(is_B_type));
  and and_14 (and_14_out, Instruction[12], Instruction[13], Instruction[14]);
  and and_15 (and_15_out, Instruction[12], ~Instruction[13], ~Instruction[14]);  // AND_Gate
  and and_16 (and_16_out, ~Instruction[25], ~Instruction[26], ~Instruction[27], ~Instruction[28], ~Instruction[29], ~Instruction[30], ~Instruction[31]);  // AND_Gate
  and and_17 (is_xori, is_I_type, and_14_out);
  and and_18 (is_slli, is_I_type, and_15_out, and_16_out);
  Multiplexer #(.width(3)) multiplexer_4 (
    .in0(multiplexer_3_out), .in1(3'b001), .out(multiplexer_4_out), .sel(is_S_type));
  Multiplexer #(.width(3)) multiplexer_5 (.in0(multiplexer_4_out), .in1(3'b000), .out(ImmSel), .sel(is_I_type));
  and and_19 (and_19_out, Instruction[12], ~Instruction[13], Instruction[14]);  // AND_Gate
  and and_20 (and_20_out, ~Instruction[25], ~Instruction[26], ~Instruction[27], ~Instruction[28], ~Instruction[29], ~Instruction[30], ~Instruction[31]);  // AND_Gate
  and and_21 (and_21_out, Instruction[12], ~Instruction[13], Instruction[14]);  // AND_Gate
  and and_22 (and_22_out, ~Instruction[25], ~Instruction[26], ~Instruction[27], ~Instruction[28], ~Instruction[29], Instruction[30], ~Instruction[31]);  // AND_Gate
  and and_23 (is_srli, is_I_type, and_19_out, and_20_out);
  and and_24 (is_srai, is_I_type, and_21_out, and_22_out);
  and and_25 (and_25_out, ~Instruction[12], Instruction[13], ~Instruction[14]);  // AND_Gate
  assign bit_extender_1_out = {{1{1'b0}}, Instruction[14:12]};  // Bit_Extender bit_extender_1
  Multiplexer #(.width(4)) multiplexer_6 (.in0(bit_extender_1_out), .in1(4'b1101), .out(ItypeSel), .sel(is_srai));
  and and_26 (is_slti, is_I_type, and_25_out);
  Multiplexer #(.width(4)) multiplexer_7 (.in1(ItypeSel), .out(ALUSel), .sel(is_I_type));  // open: in0

  // Other names for the same wires on the sheet: opcode[6:0] = Instruction[6:0]; rd[4:0] = Instruction[11:7];
  //   funct3[2:0] = Instruction[14:12]; rs1[4:0] = Instruction[19:15]; imm[11:0] = Instruction[31:20];
  //   rs2[4:0] = Instruction[24:20]; funct7[6:0] = Instruction[31:25]

  // Notes on the sheet:
  //   INPUTS to your circuit
  //   DON'T CHANGE THE LOCATIONS OF THE INPUTS AND OUTPUTS!
  //   OUTPUT from your circuit
  //   srlai特判
endmodule
